// Logisim project exercicio-1.circ as structural Verilog: 1 circuit, main circuit main
module main (
  input  A,
  input  B,
  input  C,
  output S
);

  wire not_1_out, or_1_out, or_2_out;

  or or_1 (or_1_out, A, B);
  not not_1 (not_1_out, B);
  or or_2 (or_2_out, not_1_out, C);
  and and_1 (S, or_1_out, or_2_out);
endmodule
